# Fritzing sketch WiFi_Clock_ESP32 (saved by Fritzing 1.0.5)

parts:
  U1 = ESP32-38PinWide [part_number=ESP32-38PinWide]
  IC1 = Nextion SPI 2.4" LCD NX3224T024_011

nets:
  VIN: U1.VIN, IC1.VCC
  N1: U1.GPIO16, IC1.TX
  N2: U1.GPIO17, IC1.RX
  GND: U1.GND, IC1.GND

notes:
  Nextion Pin
  VCC 5V
  RX > 17
  TX > 16
  GND

custom parts:
  ESP32-38PinWide: Generic 38-Pin ESP32 with wide format (only access to one side of pins on a breadboard) based on Stephen Lilley's HiLetgo ESP-WROOM-32 ESP32 ESP-32S Development Board.
