# Fritzing sketch WiFi_Clock_ESP8266 (saved by Fritzing 1.0.5)

parts:
  Mod1 = Amica NodeMCU DEVKIT 1.0
  IC1 = Nextion SPI 2.4" LCD NX3224T024_011

nets:
  N1: Mod1.pin7, IC1.RX
  N2: Mod1.pin8, IC1.TX
  N3: Mod1.pin_9, Mod1.pin_25, IC1.GND
  N4: Mod1.pin_30, IC1.VCC

notes:
  Nextion Pin
  VCC 5V
  TX > D5
  RX > D6
  GND
